# Fritzing sketch AudioVisualizer (saved by Fritzing 0.9.5d)
breadboards: 1

parts:
  M1 = STM32F103C8T6 blue mini board
  Part1 = LED Matrix - Serial Interface - Red/Green/Blue
  Part2 = LED Matrix - Serial Interface - Red/Green/Blue
  Part3 = LED Matrix - Serial Interface - Red/Green/Blue
  Part4 = LED Matrix - Serial Interface - Red/Green/Blue
  Part5 = Breakout Board for Electret Microphone

nets:
  VCC: M1.5V, Part1.VCC, Part2.VCC, Part3.VCC, Part4.VCC
  GND: M1.G, Part1.GND, Part2.GND, Part3.GND, Part4.GND, Part5.GND
  3.3V: M1.3.3V, Part5.VCC
  N1: M1.A0, Part5.AUD
  N2: M1.A5, Part1.SCK, Part2.SCK, Part3.SCK, Part4.SCK
  N3: M1.A6, Part1.CS, Part2.CS, Part3.CS, Part4.CS
  N4: M1.A7, Part3.MISO
  N5: Part1.MISO, Part2.MOSI
  N6: Part2.MISO, Part4.MOSI
  N7: Part3.MOSI, Part4.MISO

notes:
  You Need External 5v with at least 300mA.
